# Fritzing sketch schéma circuit (1) (saved by Fritzing 0.9.3b)
breadboards: 1

parts:
  Composant1 = Arduino Uno (Rev3)
  R1 = Resistor [tolerance=±5% resistance=10k package=THT]
  L1 = Inductor [package="400 mil [THT]"]
  C2 = Ceramic Capacitor [capacitance=10nF package="100 mil [THT, multilayer]"]
  D1 = Rectifier Diode [part_number=1N4148 package="300 mil [THT]"]
  R2 = Resistor [tolerance=±5% resistance=1M package=THT]
  C1 = Ceramic Capacitor [capacitance=0.1nF package="100 mil [THT, multilayer]"]
  R3 = Resistor [tolerance=±5% resistance=3.3k package=THT]
  R5 = Resistor [tolerance=±5% resistance=250 package=THT]
  LED1 = LED - 5mm [color="Red (633nm)" package="5 mm [THT]"]
  LED2 = LED - 5mm [color="Yellow (574nm)" package="5 mm [THT]"]
  LED3 = LED - 5mm [color="Green (555nm)" package="5 mm [THT]"]
  R6 = Resistor [tolerance=±5% resistance=250 package=THT]
  LED4 = LED - 5mm [color="Red (633nm)" package="5 mm [THT]"]
  LED5 = LED - 5mm [color="Red (633nm)" package="5 mm [THT]"]

nets:
  N1: Composant1.A0, D1.cathode, R2.Pin_1, C1.1
  N2: Composant1.D9_PWM, R1.Pin_1
  GND: Composant1.GND, R2.Pin_0, C1.0, R3.Pin_0, R5.Pin_1, LED4.cathode, LED5.cathode
  N3: Composant1.D2, R6.Pin_1
  N4: Composant1.D3_PWM, LED3.anode
  N5: Composant1.D4, LED2.anode
  N6: Composant1.D5_PWM, LED1.anode
  N7: R1.Pin_0, L1.pin_1, R3.Pin_1
  N8: L1.pin_0, C2.0, D1.anode
  Electrode: C2.1
  N9: R5.Pin_0, LED1.cathode, LED2.cathode, LED3.cathode
  N10: R6.Pin_0, LED4.anode, LED5.anode
